# Fritzing sketch sketch (saved by Fritzing 0.9.3b)
circuit board: 4.3cm x 1.7cm
breadboards: 1

parts:
  U1 = ESP8266 WiFi Module [part_number=ESP8266]
  DHT1 = DHT11 Humitidy and Temperature Sensor
  U3 = USB Connectors [package=usb-a-pcb]
  C1 = Ceramic Capacitor [capacitance=100nF package="200 mil [THT, multilayer]"]
  R1 = Resistor [tolerance=±5% resistance=4.7k package=THT]
  U4 = V_REG_LD1117VXX [package=78xxl]  # not connected

nets:
  VCC: U1.VCC, U1.RST, U1.CH_PD, DHT1.VDD, C1.0, R1.Pin_1
  N1: U1.GPIO_2, DHT1.DATA, R1.Pin_0
  GND: U1.GND, DHT1.GND, U3.GND, C1.1

custom parts:
  ESP8266 WiFi Module: Generic WiFi Module based on the ESP8266 with onboard PCB antenna and UART communications
  DHT11 Humitidy and Temperature Sensor: DHT11 Humidity and Temperature Sensor
